// Logisim project CRC.circ as structural Verilog: 2 circuits, main circuit div
module div (
  input  [3:0] in_1,
  input  [3:0] in_2,
  output [3:0] out_3
);

  wire [3:0] xor_1_out;

  assign xor_1_out = in_1 ^ in_2;  // XOR_Gate xor_1, 4 bits wide
  Multiplexer #(.width(4)) multiplexer_1 (.in0(in_1), .in1(xor_1_out), .out(out_3), .sel(in_1[3]));  // open: en
endmodule

module CRC (
  input  [7:0] in_1,
  input  [3:0] in_2,
  output [10:0] out_3
);

  wire [2:0] div_6_out_3_2;
  wire [3:0] div_1_out_3, div_2_out_3, div_3_out_3, div_4_out_3, div_5_out_3, div_7_out_3;
  wire [3:3] div_6_out_3, div_8_out_3;

  div div_1 (.in_1(in_1[7:4]), .in_2(in_2), .out_3(div_1_out_3));
  div div_2 (.in_1({div_1_out_3[2:0], in_1[3]}), .in_2(in_2), .out_3(div_2_out_3));
  div div_3 (.in_1({div_2_out_3[2:0], in_1[2]}), .in_2(in_2), .out_3(div_3_out_3));
  div div_4 (.in_1({div_3_out_3[2:0], in_1[1]}), .in_2(in_2), .out_3(div_4_out_3));
  div div_5 (.in_1({div_4_out_3[2:0], in_1[0]}), .in_2(in_2), .out_3(div_5_out_3));
  div div_6 (.in_1({div_5_out_3[2:0], 1'b0}), .in_2(in_2), .out_3({div_6_out_3[3], div_6_out_3_2}));
  div div_7 (.in_1({div_6_out_3_2, 1'b0}), .in_2(in_2), .out_3(div_7_out_3));
  div div_8 (.in_1({div_7_out_3[2:0], 1'b0}), .in_2(in_2), .out_3({div_8_out_3[3], out_3[2:0]}));

  assign out_3[10:3] = in_1;
endmodule
