// Logisim project FSM.circ as structural Verilog: 1 circuit, main circuit fsm
module fsm (
  input  [1:0] In,
  input  CLR,
  output out_3
);

  wire and_1_out, and_2_out, and_3_out, and_4_out, clock_1_out, not_1_out, not_2_out, not_3_out, not_4_out,
       not_5_out, not_6_out, not_7_out, not_8_out, not_9_out, register_1_q;
  wire [1:0] or_1_out, S_q;

  not not_1 (not_1_out, In[1]);
  not not_2 (not_2_out, In[0]);
  not not_3 (not_3_out, S_q[0]);
  not not_4 (not_4_out, S_q[1]);
  not not_5 (not_5_out, In[0]);
  not not_6 (not_6_out, S_q[0]);
  not not_7 (not_7_out, In[0]);
  and and_1 (and_1_out, In[0], not_1_out);
  and and_2 (and_2_out, not_2_out, not_3_out, S_q[1]);
  and and_3 (and_3_out, not_4_out, S_q[0], not_5_out);
  and and_4 (and_4_out, S_q[1], not_6_out, not_7_out);
  or or_1 (or_1_out[0], and_1_out, and_2_out);
  or or_2 (or_1_out[1], and_3_out, and_4_out);
  Register #(.width(2)) S (.D(or_1_out), .Q(S_q), .clk(clock_1_out), .clr(register_1_q));  // open: en
  Register #(.width(1)) register_1 (.D(CLR), .Q(register_1_q), .clk(clock_1_out), .clr(register_1_q));  // open: en
  Clock clock_1 (.out(clock_1_out));
  not not_8 (not_8_out, In[0]);
  not not_9 (not_9_out, S_q[0]);
  and and_5 (out_3, not_8_out, not_9_out, S_q[1]);
endmodule
