// Logisim project GRF.circ as structural Verilog: 1 circuit, main circuit grf
module grf (
  input  [31:0] WD,
  input  WE,
  input  [4:0] A1,
  input  [4:0] A2,
  input  [4:0] A3,
  input  in_6,
  input  in_7,
  output [31:0] RD1,
  output [31:0] RD2
);

  wire WE0, WE1, WE2, WE3, WE4, WE5, WE6, WE7, WE8, WE9, WE10, WE11, WE12, WE13, WE14, WE15, WE16, WE17,
       WE18, WE19, WE20, WE21, WE22, WE23, WE24, WE25, WE26, WE27, WE28, WE29, WE30, WE31;
  wire [31:0] i0, i1, i2, i3, i4, i5, i6, i7, i8, i9, i10, i11, i12, i13, i14, i15, i16, i17, i18, i19, i20,
       i21, i22, i23, i24, i25, i26, i27, i28, i29, i30, i31, r0, r1, r2, r3, r4, r5, r6, r7, r8, r9, r10,
       r11, r12, r13, r14, r15, r16, r17, r18, r19, r20, r21, r22, r23, r24, r25, r26, r27, r28, r29, r30,
       r31;

  Register #(.width(32)) register_1 (.D(i0), .en(1'b0), .Q(r0), .clk(in_7), .clr(in_6));
  Register #(.width(32)) register_2 (.D(i4), .en(WE4), .Q(r4), .clk(in_7), .clr(in_6));
  Register #(.width(32)) register_3 (.D(i8), .en(WE8), .Q(r8), .clk(in_7), .clr(in_6));
  Register #(.width(32)) register_4 (.D(i12), .en(WE12), .Q(r12), .clk(in_7), .clr(in_6));
  Register #(.width(32)) register_5 (.D(i16), .en(WE16), .Q(r16), .clk(in_7), .clr(in_6));
  Register #(.width(32)) register_6 (.D(i20), .en(WE20), .Q(r20), .clk(in_7), .clr(in_6));
  Register #(.width(32)) register_7 (.D(i24), .en(WE24), .Q(r24), .clk(in_7), .clr(in_6));
  Register #(.width(32)) register_8 (.D(i28), .en(WE28), .Q(r28), .clk(in_7), .clr(in_6));
  Register #(.width(32)) register_9 (.D(i1), .en(WE1), .Q(r1), .clk(in_7), .clr(in_6));
  Register #(.width(32)) register_10 (.D(i5), .en(WE5), .Q(r5), .clk(in_7), .clr(in_6));
  Register #(.width(32)) register_11 (.D(i9), .en(WE9), .Q(r9), .clk(in_7), .clr(in_6));
  Register #(.width(32)) register_12 (.D(i13), .en(WE13), .Q(r13), .clk(in_7), .clr(in_6));
  Register #(.width(32)) register_13 (.D(i17), .en(WE17), .Q(r17), .clk(in_7), .clr(in_6));
  Register #(.width(32)) register_14 (.D(i21), .en(WE21), .Q(r21), .clk(in_7), .clr(in_6));
  Register #(.width(32)) register_15 (.D(i25), .en(WE25), .Q(r25), .clk(in_7), .clr(in_6));
  Register #(.width(32)) register_16 (.D(i29), .en(WE29), .Q(r29), .clk(in_7), .clr(in_6));
  Register #(.width(32)) register_17 (.D(i2), .en(WE2), .Q(r2), .clk(in_7), .clr(in_6));
  Register #(.width(32)) register_18 (.D(i6), .en(WE6), .Q(r6), .clk(in_7), .clr(in_6));
  Register #(.width(32)) register_19 (.D(i10), .en(WE10), .Q(r10), .clk(in_7), .clr(in_6));
  Register #(.width(32)) register_20 (.D(i14), .en(WE14), .Q(r14), .clk(in_7), .clr(in_6));
  Register #(.width(32)) register_21 (.D(i18), .en(WE18), .Q(r18), .clk(in_7), .clr(in_6));
  Register #(.width(32)) register_22 (.D(i22), .en(WE22), .Q(r22), .clk(in_7), .clr(in_6));
  Register #(.width(32)) register_23 (.D(i26), .en(WE26), .Q(r26), .clk(in_7), .clr(in_6));
  Register #(.width(32)) register_24 (.D(i30), .en(WE30), .Q(r30), .clk(in_7), .clr(in_6));
  Register #(.width(32)) register_25 (.D(i3), .en(WE3), .Q(r3), .clk(in_7), .clr(in_6));
  Register #(.width(32)) register_26 (.D(i7), .en(WE7), .Q(r7), .clk(in_7), .clr(in_6));
  Register #(.width(32)) register_27 (.D(i11), .en(WE11), .Q(r11), .clk(in_7), .clr(in_6));
  Register #(.width(32)) register_28 (.D(i15), .en(WE15), .Q(r15), .clk(in_7), .clr(in_6));
  Register #(.width(32)) register_29 (.D(i19), .en(WE19), .Q(r19), .clk(in_7), .clr(in_6));
  Register #(.width(32)) register_30 (.D(i23), .en(WE23), .Q(r23), .clk(in_7), .clr(in_6));
  Register #(.width(32)) register_31 (.D(i27), .en(WE27), .Q(r27), .clk(in_7), .clr(in_6));
  Register #(.width(32)) register_32 (.D(i31), .en(WE31), .Q(r31), .clk(in_7), .clr(in_6));
  Multiplexer #(.select(5), .width(32)) multiplexer_1 (
    .in0(r0), .in1(r1), .in2(r2), .in3(r3), .in4(r4), .in5(r5), .in6(r6), .in7(r7), .in8(r8), .in9(r9),
    .in10(r10), .in11(r11), .in12(r12), .in13(r13), .in14(r14), .in15(r15), .in16(r16), .in17(r17),
    .in18(r18), .in19(r19), .in20(r20), .in21(r21), .in22(r22), .in23(r23), .in24(r24), .in25(r25),
    .in26(r26), .in27(r27), .in28(r28), .in29(r29), .in30(r30), .in31(r31), .out(RD1), .sel(A1));  // open: en
  Multiplexer #(.select(5), .width(32)) multiplexer_2 (
    .in0(r0), .in1(r1), .in2(r2), .in3(r3), .in4(r4), .in5(r5), .in6(r6), .in7(r7), .in8(r8), .in9(r9),
    .in10(r10), .in11(r11), .in12(r12), .in13(r13), .in14(r14), .in15(r15), .in16(r16), .in17(r17),
    .in18(r18), .in19(r19), .in20(r20), .in21(r21), .in22(r22), .in23(r23), .in24(r24), .in25(r25),
    .in26(r26), .in27(r27), .in28(r28), .in29(r29), .in30(r30), .in31(r31), .out(RD2), .sel(A2));  // open: en
  Demultiplexer #(.select(5), .width(32)) demultiplexer_1 (
    .out0(i0), .out1(i1), .out2(i2), .out3(i3), .out4(i4), .out5(i5), .out6(i6), .out7(i7), .out8(i8),
    .out9(i9), .out10(i10), .out11(i11), .out12(i12), .out13(i13), .out14(i14), .out15(i15), .out16(i16),
    .out17(i17), .out18(i18), .out19(i19), .out20(i20), .out21(i21), .out22(i22), .out23(i23), .out24(i24),
    .out25(i25), .out26(i26), .out27(i27), .out28(i28), .out29(i29), .out30(i30), .out31(i31), .in(WD),
    .sel(A3));  // open: en
  Demultiplexer #(.select(5)) demultiplexer_2 (
    .out0(WE0), .out1(WE1), .out2(WE2), .out3(WE3), .out4(WE4), .out5(WE5), .out6(WE6), .out7(WE7),
    .out8(WE8), .out9(WE9), .out10(WE10), .out11(WE11), .out12(WE12), .out13(WE13), .out14(WE14),
    .out15(WE15), .out16(WE16), .out17(WE17), .out18(WE18), .out19(WE19), .out20(WE20), .out21(WE21),
    .out22(WE22), .out23(WE23), .out24(WE24), .out25(WE25), .out26(WE26), .out27(WE27), .out28(WE28),
    .out29(WE29), .out30(WE30), .out31(WE31), .in(WE), .sel(A3));  // open: en

  // Other names for the same wires on the sheet: clk = in_7; reset = in_6
endmodule
