// Logisim project SingleCycleCPU_P3.circ as structural Verilog: 7 circuits, main circuit main
module IFU (
  input  [31:0] nPC,
  input  clk,
  input  reset,
  output [31:0] PC,
  output [31:0] Instr
);

  wire [31:12] PC_q;

  Register #(.width(32)) u_PC (.D(nPC), .Q({PC_q, PC[11:0]}), .clk(clk), .clr(reset));  // open: en
  ROM #(.addrWidth(5), .dataWidth(32)) rom_1 (.addr(PC[6:2]), .data(Instr));  // open: sel

  assign PC[31:12] = 20'h3;

  // Notes on the sheet:
  //   contents of rom_1 (hex, n*v repeats v):
  //   8c080000 8c090004 8c0a0008 8c0b000c 8c040010 802809 ac100010 ac110014 ac120018 ac13001c c000c13
  //   1098021 1688823 12110001 3612007b 3c12007b 36530141 0 a00008
endmodule

module GRF (
  input  [31:0] WriteData,
  input  WriteEn,
  input  [4:0] Addr1,
  input  [4:0] Addr2,
  input  [4:0] Addr3,
  input  in_6,
  input  in_7,
  output [31:0] ReadData1,
  output [31:0] ReadData2
);

  wire WE0, WE1, WE2, WE3, WE4, WE5, WE6, WE7, WE8, WE9, WE10, WE11, WE12, WE13, WE14, WE15, WE16, WE17,
       WE18, WE19, WE20, WE21, WE22, WE23, WE24, WE25, WE26, WE27, WE28, WE29, WE30, WE31;
  wire [31:0] i0, i1, i2, i3, i4, i5, i6, i7, i8, i9, i10, i11, i12, i13, i14, i15, i16, i17, i18, i19, i20,
       i21, i22, i23, i24, i25, i26, i27, i28, i29, i30, i31, r0, r1, r2, r3, r4, r5, r6, r7, r8, r9, r10,
       r11, r12, r13, r14, r15, r16, r17, r18, r19, r20, r21, r22, r23, r24, r25, r26, r27, r28, r29, r30,
       r31;

  Register #(.width(32)) register_1 (.D(i0), .en(1'b0), .Q(r0), .clk(in_7), .clr(in_6));
  Register #(.width(32)) register_2 (.D(i4), .en(WE4), .Q(r4), .clk(in_7), .clr(in_6));
  Register #(.width(32)) register_3 (.D(i8), .en(WE8), .Q(r8), .clk(in_7), .clr(in_6));
  Register #(.width(32)) register_4 (.D(i12), .en(WE12), .Q(r12), .clk(in_7), .clr(in_6));
  Register #(.width(32)) register_5 (.D(i16), .en(WE16), .Q(r16), .clk(in_7), .clr(in_6));
  Register #(.width(32)) register_6 (.D(i20), .en(WE20), .Q(r20), .clk(in_7), .clr(in_6));
  Register #(.width(32)) register_7 (.D(i24), .en(WE24), .Q(r24), .clk(in_7), .clr(in_6));
  Register #(.width(32)) register_8 (.D(i28), .en(WE28), .Q(r28), .clk(in_7), .clr(in_6));
  Register #(.width(32)) register_9 (.D(i1), .en(WE1), .Q(r1), .clk(in_7), .clr(in_6));
  Register #(.width(32)) register_10 (.D(i5), .en(WE5), .Q(r5), .clk(in_7), .clr(in_6));
  Register #(.width(32)) register_11 (.D(i9), .en(WE9), .Q(r9), .clk(in_7), .clr(in_6));
  Register #(.width(32)) register_12 (.D(i13), .en(WE13), .Q(r13), .clk(in_7), .clr(in_6));
  Register #(.width(32)) register_13 (.D(i17), .en(WE17), .Q(r17), .clk(in_7), .clr(in_6));
  Register #(.width(32)) register_14 (.D(i21), .en(WE21), .Q(r21), .clk(in_7), .clr(in_6));
  Register #(.width(32)) register_15 (.D(i25), .en(WE25), .Q(r25), .clk(in_7), .clr(in_6));
  Register #(.width(32)) register_16 (.D(i29), .en(WE29), .Q(r29), .clk(in_7), .clr(in_6));
  Register #(.width(32)) register_17 (.D(i2), .en(WE2), .Q(r2), .clk(in_7), .clr(in_6));
  Register #(.width(32)) register_18 (.D(i6), .en(WE6), .Q(r6), .clk(in_7), .clr(in_6));
  Register #(.width(32)) register_19 (.D(i10), .en(WE10), .Q(r10), .clk(in_7), .clr(in_6));
  Register #(.width(32)) register_20 (.D(i14), .en(WE14), .Q(r14), .clk(in_7), .clr(in_6));
  Register #(.width(32)) register_21 (.D(i18), .en(WE18), .Q(r18), .clk(in_7), .clr(in_6));
  Register #(.width(32)) register_22 (.D(i22), .en(WE22), .Q(r22), .clk(in_7), .clr(in_6));
  Register #(.width(32)) register_23 (.D(i26), .en(WE26), .Q(r26), .clk(in_7), .clr(in_6));
  Register #(.width(32)) register_24 (.D(i30), .en(WE30), .Q(r30), .clk(in_7), .clr(in_6));
  Register #(.width(32)) register_25 (.D(i3), .en(WE3), .Q(r3), .clk(in_7), .clr(in_6));
  Register #(.width(32)) register_26 (.D(i7), .en(WE7), .Q(r7), .clk(in_7), .clr(in_6));
  Register #(.width(32)) register_27 (.D(i11), .en(WE11), .Q(r11), .clk(in_7), .clr(in_6));
  Register #(.width(32)) register_28 (.D(i15), .en(WE15), .Q(r15), .clk(in_7), .clr(in_6));
  Register #(.width(32)) register_29 (.D(i19), .en(WE19), .Q(r19), .clk(in_7), .clr(in_6));
  Register #(.width(32)) register_30 (.D(i23), .en(WE23), .Q(r23), .clk(in_7), .clr(in_6));
  Register #(.width(32)) register_31 (.D(i27), .en(WE27), .Q(r27), .clk(in_7), .clr(in_6));
  Register #(.width(32)) register_32 (.D(i31), .en(WE31), .Q(r31), .clk(in_7), .clr(in_6));
  Multiplexer #(.select(5), .width(32)) multiplexer_1 (
    .in0(r0), .in1(r1), .in2(r2), .in3(r3), .in4(r4), .in5(r5), .in6(r6), .in7(r7), .in8(r8), .in9(r9),
    .in10(r10), .in11(r11), .in12(r12), .in13(r13), .in14(r14), .in15(r15), .in16(r16), .in17(r17),
    .in18(r18), .in19(r19), .in20(r20), .in21(r21), .in22(r22), .in23(r23), .in24(r24), .in25(r25),
    .in26(r26), .in27(r27), .in28(r28), .in29(r29), .in30(r30), .in31(r31), .out(ReadData1), .sel(Addr1));  // open: en
  Multiplexer #(.select(5), .width(32)) multiplexer_2 (
    .in0(r0), .in1(r1), .in2(r2), .in3(r3), .in4(r4), .in5(r5), .in6(r6), .in7(r7), .in8(r8), .in9(r9),
    .in10(r10), .in11(r11), .in12(r12), .in13(r13), .in14(r14), .in15(r15), .in16(r16), .in17(r17),
    .in18(r18), .in19(r19), .in20(r20), .in21(r21), .in22(r22), .in23(r23), .in24(r24), .in25(r25),
    .in26(r26), .in27(r27), .in28(r28), .in29(r29), .in30(r30), .in31(r31), .out(ReadData2), .sel(Addr2));  // open: en
  Demultiplexer #(.select(5), .width(32)) demultiplexer_1 (
    .out0(i0), .out1(i1), .out2(i2), .out3(i3), .out4(i4), .out5(i5), .out6(i6), .out7(i7), .out8(i8),
    .out9(i9), .out10(i10), .out11(i11), .out12(i12), .out13(i13), .out14(i14), .out15(i15), .out16(i16),
    .out17(i17), .out18(i18), .out19(i19), .out20(i20), .out21(i21), .out22(i22), .out23(i23), .out24(i24),
    .out25(i25), .out26(i26), .out27(i27), .out28(i28), .out29(i29), .out30(i30), .out31(i31),
    .in(WriteData), .sel(Addr3));  // open: en
  Demultiplexer #(.select(5)) demultiplexer_2 (
    .out0(WE0), .out1(WE1), .out2(WE2), .out3(WE3), .out4(WE4), .out5(WE5), .out6(WE6), .out7(WE7),
    .out8(WE8), .out9(WE9), .out10(WE10), .out11(WE11), .out12(WE12), .out13(WE13), .out14(WE14),
    .out15(WE15), .out16(WE16), .out17(WE17), .out18(WE18), .out19(WE19), .out20(WE20), .out21(WE21),
    .out22(WE22), .out23(WE23), .out24(WE24), .out25(WE25), .out26(WE26), .out27(WE27), .out28(WE28),
    .out29(WE29), .out30(WE30), .out31(WE31), .in(WriteEn), .sel(Addr3));  // open: en

  // Other names for the same wires on the sheet: clk = in_7; reset = in_6
endmodule

module ALU (
  input  [31:0] A,
  input  [31:0] B,
  input  [2:0] ALUOp,
  output Zero,
  output [31:0] ALUResult
);

  wire [31:0] adder_1_out, and_1_out, or_1_out, subtractor_1_out;

  Adder #(.width(32)) adder_1 (.a(A), .b(B), .out(adder_1_out));  // open: cin, cout
  Subtractor #(.width(32)) subtractor_1 (.a(A), .b(B), .out(subtractor_1_out));  // open: bin, bout
  assign and_1_out = A & B;  // AND_Gate and_1, 32 bits wide
  assign or_1_out = A | B;  // OR_Gate or_1, 32 bits wide
  Multiplexer #(.select(3), .width(32)) multiplexer_1 (
    .in0(adder_1_out), .in1(subtractor_1_out), .in2(and_1_out), .in3(or_1_out), .out(ALUResult), .sel(ALUOp));  // open: in4, in5, in6, in7, en
  Comparator #(.width(32)) comparator_1 (.a({32{1'b0}}), .b(ALUResult), .eq(Zero));  // open: gt, lt
endmodule

module DM (
  input  [4:0] Addr,
  input  [31:0] WriteData,
  input  WriteEn,
  input  clk,
  input  reset,
  output [31:0] ReadData
);

  RAM #(.addrWidth(5), .dataWidth(32), .bus("separate")) ram_1 (
    .addr(Addr), .din(WriteData), .data(ReadData), .str(WriteEn), .clk(clk), .clr(reset));  // open: sel, ld
endmodule

module main (
  input  Reset,
  output [31:0] out_2,
  output out_3,
  output [4:0] out_4,
  output [31:0] out_5,
  output out_6,
  output [4:0] out_7,
  output [31:0] out_8
);

  wire alu_1_zero, clock_1_out, ctrl_1_alusrc, ctrl_1_extop;
  wire [1:0] ctrl_1_npcsrc, ctrl_1_regdst, ctrl_1_regsrc;
  wire [2:0] ctrl_1_aluop;
  wire [27:0] adder_1_out;
  wire [31:0] adder_2_out, alu_1_aluresult, dm_1_readdata, ext_1_dst, grf_1_readdata1, ifu_1_pc,
       multiplexer_1_out, multiplexer_2_out, multiplexer_4_out, shifter_1_out;
  wire [31:28] adder_1_out_2;

  Clock clock_1 (.out(clock_1_out));
  Multiplexer #(.width(32), .enable("false")) multiplexer_1 (
    .in0({adder_1_out_2, adder_1_out}), .in1(adder_2_out), .out(multiplexer_1_out), .sel(alu_1_zero));
  Multiplexer #(.select(2), .width(32), .enable("false")) multiplexer_2 (
    .in0({adder_1_out_2, adder_1_out}), .in1(multiplexer_1_out), .in2({adder_1_out_2, out_2[25:0], 2'b00}),
    .in3(grf_1_readdata1), .out(multiplexer_2_out), .sel(ctrl_1_npcsrc));
  IFU ifu_1 (.nPC(multiplexer_2_out), .clk(clock_1_out), .Instr(out_2), .reset(Reset), .PC(ifu_1_pc));
  Multiplexer #(.select(2), .width(5), .enable("false")) multiplexer_3 (
    .in0(out_2[20:16]), .in1(out_2[15:11]), .in2({5{1'b1}}), .out(out_4), .sel(ctrl_1_regdst));  // open: in3
  Adder #(.width(32)) adder_1 (.a(ifu_1_pc), .b(32'h4), .out({adder_1_out_2, adder_1_out}));  // open: cin, cout
  Ctrl ctrl_1 (
    .Funct(out_2[5:0]), .Op(out_2[31:26]), .nPCSrc(ctrl_1_npcsrc), .RegSrc(ctrl_1_regsrc),
    .ALUOp(ctrl_1_aluop), .RegDst(ctrl_1_regdst), .MemWrite(out_6), .ALUSrc(ctrl_1_alusrc),
    .ExtOp(ctrl_1_extop), .RegWrite(out_3));
  GRF grf_1 (
    .WriteData(out_5), .WriteEn(out_3), .in_6(Reset), .in_7(clock_1_out), .ReadData1(grf_1_readdata1),
    .ReadData2(out_8), .Addr1(out_2[25:21]), .Addr2(out_2[20:16]), .Addr3(out_4));
  Ext ext_1 (.Src(out_2[15:0]), .ExtOp(ctrl_1_extop), .Dst(ext_1_dst));
  Multiplexer #(.width(32), .enable("false")) multiplexer_4 (
    .in0(out_8), .in1(ext_1_dst), .out(multiplexer_4_out), .sel(ctrl_1_alusrc));
  Shifter #(.width(32)) shifter_1 (.in(ext_1_dst), .\dist (5'b00010), .out(shifter_1_out));
  ALU alu_1 (
    .A(grf_1_readdata1), .B(multiplexer_4_out), .ALUOp(ctrl_1_aluop), .Zero(alu_1_zero),
    .ALUResult({alu_1_aluresult[31:7], out_7, alu_1_aluresult[1:0]}));
  Adder #(.width(32)) adder_2 (
    .a(shifter_1_out), .b({adder_1_out_2, adder_1_out}), .out(adder_2_out));  // open: cin, cout
  DM dm_1 (
    .Addr(out_7), .WriteData(out_8), .WriteEn(out_6), .clk(clock_1_out), .reset(Reset),
    .ReadData(dm_1_readdata));
  Multiplexer #(.select(2), .width(32), .enable("false")) multiplexer_5 (
    .in0({alu_1_aluresult[31:7], out_7, alu_1_aluresult[1:0]}), .in1(dm_1_readdata),
    .in2({out_2[15:0], {16{1'b0}}}), .in3({adder_1_out_2, adder_1_out}), .out(out_5), .sel(ctrl_1_regsrc));

  // Other names for the same wires on the sheet: MemAddr[4:0] = out_7; Instr[31:0] = out_2; MemData[31:0] = out_8;
  //   MemWrite = out_6; RegAddr[4:0] = out_4; RegData[31:0] = out_5; RegWrite = out_3
endmodule

module Ext (
  input  [15:0] Src,
  input  ExtOp,
  output [31:0] Dst
);

  wire [31:0] bit_extender_1_out, bit_extender_2_out;

  assign bit_extender_1_out = {{16{Src[15]}}, Src};  // Bit_Extender bit_extender_1
  assign bit_extender_2_out = {{16{1'b0}}, Src};  // Bit_Extender bit_extender_2
  Multiplexer #(.width(32), .enable("false")) multiplexer_1 (
    .in0(bit_extender_1_out), .in1(bit_extender_2_out), .out(Dst), .sel(ExtOp));
endmodule

module Ctrl (
  input  [5:0] Funct,
  input  [5:0] Op,
  output MemWrite,
  output ALUSrc,
  output ExtOp,
  output RegWrite,
  output [1:0] nPCSrc,
  output [1:0] RegSrc,
  output [2:0] ALUOp,
  output [1:0] RegDst
);

  wire addu_out, beq_out, j_out, jalr_out, jr_out, lui_out, lw_out, not_1_out, not_2_out, not_3_out,
       not_4_out, not_5_out, not_6_out, not_7_out, not_8_out, not_9_out, not_10_out, not_11_out, not_12_out,
       subu_out;

  not not_1 (not_1_out, Funct[4]);
  not not_2 (not_2_out, Funct[5]);
  not not_3 (not_3_out, Funct[3]);
  not not_4 (not_4_out, Funct[2]);
  not not_5 (not_5_out, Funct[1]);
  not not_6 (not_6_out, Funct[0]);
  not not_7 (not_7_out, Op[5]);
  not not_8 (not_8_out, Op[4]);
  not not_9 (not_9_out, Op[3]);
  not not_10 (not_10_out, Op[1]);
  not not_11 (not_11_out, Op[2]);
  not not_12 (not_12_out, Op[0]);
  and addu (addu_out, not_7_out, not_8_out, not_9_out, not_11_out, not_10_out, not_12_out, Funct[5], not_1_out, not_3_out, not_4_out, not_5_out, Funct[0]);
  and subu (subu_out, not_7_out, not_8_out, not_9_out, not_11_out, not_10_out, not_12_out, Funct[5], not_1_out, not_3_out, not_4_out, Funct[1], Funct[0]);
  and ori (ALUOp[1], not_7_out, not_8_out, Op[3], Op[2], not_10_out, Op[0]);
  and lw (lw_out, Op[5], not_8_out, not_9_out, not_11_out, Op[1], Op[0]);
  and sw (MemWrite, Op[5], not_8_out, Op[3], not_11_out, Op[1], Op[0]);
  and beq (beq_out, not_7_out, not_8_out, not_9_out, Op[2], not_10_out, not_12_out);
  and lui (lui_out, not_7_out, not_8_out, Op[3], Op[2], Op[1], Op[0]);
  and jal (RegDst[1], not_7_out, not_8_out, not_9_out, not_11_out, Op[1], Op[0]);
  and jr (jr_out, not_7_out, not_8_out, not_9_out, not_11_out, not_10_out, not_12_out, not_2_out, not_1_out, Funct[3], not_4_out, not_5_out, not_6_out);
  and j (j_out, not_7_out, not_8_out, not_9_out, not_11_out, Op[1], not_12_out);
  and jalr (jalr_out, not_7_out, not_8_out, not_9_out, not_11_out, not_10_out, not_12_out, not_2_out, not_1_out, Funct[3], not_4_out, not_5_out, Funct[0]);
  or or_1 (nPCSrc[1], RegDst[1], j_out, jalr_out, jr_out);
  or or_2 (RegSrc[1], lui_out, jalr_out, RegDst[1]);
  or or_3 (nPCSrc[0], beq_out, jalr_out, jr_out);
  or or_4 (RegSrc[0], lw_out, jalr_out, RegDst[1]);
  or or_5 (ALUOp[0], subu_out, ALUOp[1], beq_out);
  or or_6 (ALUSrc, ALUOp[1], lw_out, MemWrite);
  or or_7 (RegDst[0], addu_out, jalr_out, subu_out);
  or or_8 (RegWrite, addu_out, subu_out, ALUOp[1], jalr_out, lw_out, lui_out, RegDst[1]);

  assign ALUOp[2] = 1'b0;
  assign ExtOp = ALUOp[1];
endmodule
