// Logisim project fib2.circ as structural Verilog: 3 circuits, main circuit main
// 1
module main (
  input  [31:0] in_1,
  output [31:0] out_2
);

  wire clock_1_out, comparator_1_eq, comparator_2_gt, comparator_3_gt, comparator_4_gt;
  wire [31:0] divider_1_out, divider_1_rem, matrix_multiplier_1_out_9, matrix_multiplier_1_out_10,
       matrix_multiplier_1_out_11, matrix_multiplier_1_out_12, matrix_square_1_out_5, matrix_square_1_out_6,
       matrix_square_1_out_7, matrix_square_1_out_8, multiplexer_1_out, multiplexer_2_out, multiplexer_3_out,
       multiplexer_4_out, multiplexer_5_out, multiplexer_6_out, multiplexer_7_out, multiplexer_8_out,
       multiplexer_9_out, register_1_q, register_2_q, register_3_q, register_4_q, register_5_q, register_6_q,
       register_7_q, register_8_q, register_9_q;

  Clock clock_1 (.out(clock_1_out));
  Register #(.width(32)) register_1 (.D(divider_1_out), .Q(register_1_q), .clk(clock_1_out));  // open: en, clr
  Multiplexer #(.width(32)) multiplexer_1 (
    .in0(in_1), .in1(register_1_q), .out(multiplexer_1_out), .sel(comparator_3_gt));  // open: en
  Divider #(.width(32)) divider_1 (
    .a(multiplexer_1_out), .b(32'h2), .out(divider_1_out), .rem(divider_1_rem));  // open: upper
  Comparator #(.width(32), .mode("unsigned")) comparator_1 (
    .a(divider_1_rem), .b(32'h1), .eq(comparator_1_eq));  // open: gt, lt
  Comparator #(.width(32), .mode("unsigned")) comparator_2 (
    .a(register_4_q), .b({32{1'b0}}), .gt(comparator_2_gt));  // open: eq, lt
  Comparator #(.width(32), .mode("unsigned")) comparator_3 (
    .a(register_6_q), .b({32{1'b0}}), .gt(comparator_3_gt));  // open: eq, lt
  Comparator #(.width(32), .mode("unsigned")) comparator_4 (
    .a(multiplexer_1_out), .b({32{1'b0}}), .gt(comparator_4_gt));  // open: eq, lt
  Register #(.width(32)) register_2 (
    .D(matrix_multiplier_1_out_9), .en(comparator_1_eq), .Q(register_2_q), .clk(clock_1_out));  // open: clr
  Register #(.width(32)) register_3 (
    .D(matrix_multiplier_1_out_10), .en(comparator_1_eq), .Q(register_3_q), .clk(clock_1_out));  // open: clr
  Register #(.width(32)) register_4 (
    .D(matrix_multiplier_1_out_11), .en(comparator_1_eq), .Q(register_4_q), .clk(clock_1_out));  // open: clr
  Register #(.width(32)) register_5 (
    .D(matrix_multiplier_1_out_12), .en(comparator_1_eq), .Q(register_5_q), .clk(clock_1_out));  // open: clr
  Register #(.width(32)) register_6 (.D(matrix_square_1_out_5), .Q(register_6_q), .clk(clock_1_out));  // open: en, clr
  Register #(.width(32)) register_7 (.D(matrix_square_1_out_6), .Q(register_7_q), .clk(clock_1_out));  // open: en, clr
  Register #(.width(32)) register_8 (.D(matrix_square_1_out_7), .Q(register_8_q), .clk(clock_1_out));  // open: en, clr
  Register #(.width(32)) register_9 (.D(matrix_square_1_out_8), .Q(register_9_q), .clk(clock_1_out));  // open: en, clr
  Multiplexer #(.width(32)) multiplexer_2 (
    .in0(32'h1), .in1(register_2_q), .out(multiplexer_2_out), .sel(comparator_2_gt));  // open: en
  Multiplexer #(.width(32)) multiplexer_3 (
    .in0({32{1'b0}}), .in1(register_3_q), .out(multiplexer_3_out), .sel(comparator_2_gt));  // open: en
  Multiplexer #(.width(32)) multiplexer_4 (
    .in0({32{1'b0}}), .in1(register_4_q), .out(multiplexer_4_out), .sel(comparator_2_gt));  // open: en
  Multiplexer #(.width(32)) multiplexer_5 (
    .in0(32'h1), .in1(register_5_q), .out(multiplexer_5_out), .sel(comparator_2_gt));  // open: en
  Multiplexer #(.width(32)) multiplexer_6 (
    .in0(32'h1), .in1(register_6_q), .out(multiplexer_6_out), .sel(comparator_3_gt));  // open: en
  Multiplexer #(.width(32)) multiplexer_7 (
    .in0(32'h1), .in1(register_7_q), .out(multiplexer_7_out), .sel(comparator_3_gt));  // open: en
  Multiplexer #(.width(32)) multiplexer_8 (
    .in0(32'h1), .in1(register_8_q), .out(multiplexer_8_out), .sel(comparator_3_gt));  // open: en
  Multiplexer #(.width(32)) multiplexer_9 (
    .in0({32{1'b0}}), .in1(register_9_q), .out(multiplexer_9_out), .sel(comparator_3_gt));  // open: en
  matrix_multiplier matrix_multiplier_1 (
    .in_1(multiplexer_2_out), .in_2(multiplexer_3_out), .in_3(multiplexer_4_out), .in_4(multiplexer_5_out),
    .in_5(multiplexer_6_out), .in_6(multiplexer_7_out), .in_7(multiplexer_8_out), .in_8(multiplexer_9_out),
    .out_9(matrix_multiplier_1_out_9), .out_10(matrix_multiplier_1_out_10),
    .out_11(matrix_multiplier_1_out_11), .out_12(matrix_multiplier_1_out_12));
  matrix_square matrix_square_1 (
    .in_1(multiplexer_6_out), .in_2(multiplexer_7_out), .in_3(multiplexer_8_out), .in_4(multiplexer_9_out),
    .out_5(matrix_square_1_out_5), .out_6(matrix_square_1_out_6), .out_7(matrix_square_1_out_7),
    .out_8(matrix_square_1_out_8));
  Multiplexer #(.width(32)) multiplexer_10 (
    .in0(multiplexer_3_out), .in1({32{1'b0}}), .out(out_2), .sel(comparator_4_gt));  // open: en
endmodule

module matrix_square (
  input  [31:0] in_1,
  input  [31:0] in_2,
  input  [31:0] in_3,
  input  [31:0] in_4,
  output [31:0] out_5,
  output [31:0] out_6,
  output [31:0] out_7,
  output [31:0] out_8
);

  wire [31:0] multiplier_1_out, multiplier_2_out, multiplier_3_out, multiplier_4_out, multiplier_5_out,
       multiplier_6_out, multiplier_7_out, multiplier_8_out;

  Multiplier #(.width(32)) multiplier_1 (.a(in_1), .b(in_1), .out(multiplier_1_out));  // open: cin, cout
  Multiplier #(.width(32)) multiplier_2 (.a(in_2), .b(in_3), .out(multiplier_2_out));  // open: cin, cout
  Multiplier #(.width(32)) multiplier_3 (.a(in_1), .b(in_2), .out(multiplier_3_out));  // open: cin, cout
  Multiplier #(.width(32)) multiplier_4 (.a(in_2), .b(in_4), .out(multiplier_4_out));  // open: cin, cout
  Multiplier #(.width(32)) multiplier_5 (.a(in_1), .b(in_3), .out(multiplier_5_out));  // open: cin, cout
  Multiplier #(.width(32)) multiplier_6 (.a(in_3), .b(in_4), .out(multiplier_6_out));  // open: cin, cout
  Multiplier #(.width(32)) multiplier_7 (.a(in_2), .b(in_3), .out(multiplier_7_out));  // open: cin, cout
  Multiplier #(.width(32)) multiplier_8 (.a(in_4), .b(in_4), .out(multiplier_8_out));  // open: cin, cout
  Adder #(.width(32)) adder_1 (.a(multiplier_1_out), .b(multiplier_2_out), .out(out_5));  // open: cin, cout
  Adder #(.width(32)) adder_2 (.a(multiplier_3_out), .b(multiplier_4_out), .out(out_6));  // open: cin, cout
  Adder #(.width(32)) adder_3 (.a(multiplier_5_out), .b(multiplier_6_out), .out(out_7));  // open: cin, cout
  Adder #(.width(32)) adder_4 (.a(multiplier_7_out), .b(multiplier_8_out), .out(out_8));  // open: cin, cout
endmodule

module matrix_multiplier (
  input  [31:0] in_1,
  input  [31:0] in_2,
  input  [31:0] in_3,
  input  [31:0] in_4,
  input  [31:0] in_5,
  input  [31:0] in_6,
  input  [31:0] in_7,
  input  [31:0] in_8,
  output [31:0] out_9,
  output [31:0] out_10,
  output [31:0] out_11,
  output [31:0] out_12
);

  wire [31:0] multiplier_1_out, multiplier_2_out, multiplier_3_out, multiplier_4_out, multiplier_5_out,
       multiplier_6_out, multiplier_7_out, multiplier_8_out;

  Multiplier #(.width(32)) multiplier_1 (.a(in_1), .b(in_5), .out(multiplier_1_out));  // open: cin, cout
  Adder #(.width(32)) adder_1 (.a(multiplier_1_out), .b(multiplier_2_out), .out(out_9));  // open: cin, cout
  Multiplier #(.width(32)) multiplier_2 (.a(in_2), .b(in_7), .out(multiplier_2_out));  // open: cin, cout
  Multiplier #(.width(32)) multiplier_3 (.a(in_1), .b(in_6), .out(multiplier_3_out));  // open: cin, cout
  Adder #(.width(32)) adder_2 (.a(multiplier_3_out), .b(multiplier_4_out), .out(out_10));  // open: cin, cout
  Multiplier #(.width(32)) multiplier_4 (.a(in_2), .b(in_8), .out(multiplier_4_out));  // open: cin, cout
  Multiplier #(.width(32)) multiplier_5 (.a(in_3), .b(in_5), .out(multiplier_5_out));  // open: cin, cout
  Adder #(.width(32)) adder_3 (.a(multiplier_5_out), .b(multiplier_6_out), .out(out_11));  // open: cin, cout
  Multiplier #(.width(32)) multiplier_6 (.a(in_4), .b(in_7), .out(multiplier_6_out));  // open: cin, cout
  Multiplier #(.width(32)) multiplier_7 (.a(in_3), .b(in_6), .out(multiplier_7_out));  // open: cin, cout
  Adder #(.width(32)) adder_4 (.a(multiplier_7_out), .b(multiplier_8_out), .out(out_12));  // open: cin, cout
  Multiplier #(.width(32)) multiplier_8 (.a(in_4), .b(in_8), .out(multiplier_8_out));  // open: cin, cout
endmodule
