// Logisim project mod5.circ as structural Verilog: 1 circuit, main circuit mod5
module mod5 (
  input  in_1,
  output out_2,
  output out_3,
  output out_4,
  output out_5,
  output out_6
);

  wire clock_1_out, comparator_1_eq, not_1_out, or_1_out, or_2_out, register_2_q;
  wire [4:0] multiplexer_1_out, register_1_q;

  not not_1 (not_1_out, in_1);
  or or_1 (or_1_out, multiplexer_1_out[0], multiplexer_1_out[1], multiplexer_1_out[4]);
  or or_2 (or_2_out, multiplexer_1_out[2], multiplexer_1_out[3]);
  and and_1 (out_3, or_1_out, not_1_out);
  and and_2 (out_4, or_1_out, in_1);
  and and_3 (out_5, or_2_out, in_1);
  and and_4 (out_6, or_2_out, not_1_out);
  Register #(.width(5)) register_1 (
    .D({out_6, out_5, out_4, out_3, 1'b0}), .Q(register_1_q), .clk(clock_1_out));  // open: en, clr
  Clock clock_1 (.out(clock_1_out));
  Multiplexer #(.width(5)) multiplexer_1 (
    .in0(register_1_q), .in1(5'b00001), .out(multiplexer_1_out), .sel(comparator_1_eq));  // open: en
  Register #(.width(1)) register_2 (.D(1'b1), .Q(register_2_q), .clk(clock_1_out));  // open: en, clr
  Comparator #(.width(1)) comparator_1 (.a(1'b0), .b(register_2_q), .eq(comparator_1_eq));  // open: gt, lt

  assign out_2 = 1'b0;
endmodule
